# Fritzing sketch Montage vue generale (saved by Fritzing 0.9.3b)

parts:
  Composant1 = Arduino Mega 2560 (Rev3)
  HC-SR04_Sensor_1 = HC-SR04 Ultrasonic Distance Sensor
  HC-SR04_Sensor_2 = HC-SR04 Ultrasonic Distance Sensor
  HC-SR04_Sensor_4 = HC-SR04 Ultrasonic Distance Sensor
  M6 = fc-51 [package=THT]
  VCC1 = Battery block 9V  # not connected
  BAT1 = 12 battery [package=battery]
  L298N1 = L298N DC motor driver
  L298N2 = L298N DC motor driver
  M7 = fc-51 [package=THT]
  M8 = fc-51 [package=THT]
  HC-SR04_Sensor_5 = HC-SR04 Ultrasonic Distance Sensor
  M11 = DC Motor
  M12 = DC Motor
  M13 = DC Motor
  M14 = DC Motor
  BT1 = Bluetooth HC-06u [package=THT]

nets:
  GND: Composant1.GND, HC-SR04_Sensor_1.GND, HC-SR04_Sensor_2.GND, HC-SR04_Sensor_4.GND, HC-SR04_Sensor_5.GND, BT1.GND
  N1: Composant1.D11_PWM, BT1.RXD
  N2: Composant1.D10_PWM, BT1.TXD
  N3: Composant1.D8_PWM, M7.pin1
  3V3: Composant1.3V3, BT1.VCC
  VCC: Composant1.5V, HC-SR04_Sensor_4.VCC, HC-SR04_Sensor_5.VCC
  N4: Composant1.D2_PWM, L298N1.ENB
  N5: Composant1.D3_PWM, L298N1.ENA
  N6: Composant1.D4_PWM, L298N2.ENA
  N7: Composant1.D5_PWM, L298N2.ENB
  N8: Composant1.D6_PWM, M6.pin1
  N9: Composant1.D7_PWM, M8.pin1
  N10: Composant1.D23, L298N1.IN4
  N11: Composant1.D24, L298N1.IN3
  N12: Composant1.D26, L298N1.IN1
  N13: Composant1.D27, L298N1.IN2
  N14: Composant1.D29, L298N2.IN1
  N15: Composant1.D30, L298N2.IN2
  N16: Composant1.D31, M7.pin2
  N17: Composant1.D32, L298N2.IN4
  N18: Composant1.D33, L298N2.IN3
  N19: Composant1.D34, M6.pin3
  N20: Composant1.D36, M8.pin3
  N21: Composant1.D37, M8.pin2
  N22: Composant1.D38, M7.pin3
  N23: Composant1.D39, M6.pin2
  N24: Composant1.D40, HC-SR04_Sensor_2.VCC
  N25: Composant1.D42, HC-SR04_Sensor_5.ECHO
  N26: Composant1.D43, HC-SR04_Sensor_5.TRIG
  N27: Composant1.D44, HC-SR04_Sensor_4.ECHO
  N28: Composant1.D45, HC-SR04_Sensor_4.TRIG
  N29: Composant1.D46, HC-SR04_Sensor_2.ECHO
  N30: Composant1.D47, HC-SR04_Sensor_2.TRIG
  N31: Composant1.D48, HC-SR04_Sensor_1.ECHO
  N32: Composant1.D49, HC-SR04_Sensor_1.TRIG
  N33: Composant1.D52, HC-SR04_Sensor_1.VCC
  N34: BAT1.-, L298N2.GND
  N35: BAT1.+, L298N2.12V
  N36: L298N1.OUT1, M13.pin_2
  N37: L298N1.OUT2, M13.pin_1
  N38: L298N1.OUT3, M14.pin_2
  N39: L298N1.OUT4, M14.pin_1
  N40: L298N2.OUT1, M11.pin_2
  N41: L298N2.OUT2, M11.pin_1
  N42: L298N2.OUT3, M12.pin_2
  N43: L298N2.OUT4, M12.pin_1

custom parts:
  12 battery: 12V lead acid type battery, like the Husqvarna YTH2448 12V 35AH battery. This is the mini version 1/4 the size of the actual battery to be closer to typical breadboard parts (around 2in wide rathher than 7in). The pads in pcb are sized to accomidate up to 14ga wire (as these batterys will deliver high currents.)
  L298N DC motor driver: 2x DC motor driver with 78M05 positive voltage regulator (7..35 V) L298N: max 46 V, 2 A Set 5 V Enable jumper to enable 5 V regultor (needed for the L298N) and +5 V output at screw terminal or supply external +5 V at screw terminal Set ENA and/or ENB to +5 V to enable motor permanently or supply ENA and/or ENB with PWM signal IN1 and IN2 set rotation directory for motor A (OUT1/OUT2) IN2 and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
  Bluetooth HC-06u: Bluetooth HC-06 - face up, pins down 16.5mm x 37.5mm PCB
